# Fritzing sketch Android WiFi Robot (saved by Fritzing 0.9.3b)
breadboards: 1

parts:
  U3 = NodeMCU V1.0
  IC1 = L293D [package=THT]
  RIGHT_Motor = DC Motor
  LEFT_Motor = DC Motor
  S2 = Momentary Switch [package=ksa_sealed_tac_switch]
  External = Power Jack [part_number="POWER 9V" package=power_jack_smd]
  C1 = Capacitor [package=cap-pth-5mm]
  C2 = Capacitor [package=cap-pth-5mm]

nets:
  N1: U3.D0, S2.4
  N2: U3.D3, IC1.In_2
  N3: U3.D4, IC1.In_1
  GND: U3.GND, S2.2, External.GND
  N4: U3.D5, IC1.Enable_2
  N5: U3.D6, IC1.Enable_1
  N6: U3.D7, IC1.In_4
  N7: U3.D8, IC1.In_3
  N8: U3.Vin, IC1.+V
  N9: IC1.Out_1_(_Controlled_by_Enable_1_), LEFT_Motor.pin_1, C2.2
  N10: IC1.Out_2_(_Controlled_by_Enable_1_), LEFT_Motor.pin_2, C2.1
  N11: IC1.+Vmotor, External.GNDBREAK
  N12: IC1.Out_3_(_Controlled_by_Enable_2_), RIGHT_Motor.pin_2, C1.2
  N13: IC1.Out_4_(_Controlled_by_Enable_2_), RIGHT_Motor.pin_1, C1.1

custom parts:
  NodeMCU V1.0: ESP8266 based NodeMCU
